// Logisim project cpu.circ as structural Verilog: 5 circuits, main circuit main
// CPU
module main (
  input  [31:0] RS_READ_VALUE,
  input  [31:0] RI_READ_VALUE,
  input  [31:0] RD_READ_VALUE,
  input  [31:0] JC_READ_VALUE,
  input  [31:0] INSTRUCTION,
  input  CLOCK,
  output [4:0] RS,
  output [4:0] RI,
  output [4:0] RD,
  output [31:0] RD_WRITE_VALUE,
  output RD_WRITE_ENABLE,
  output [23:0] FETCH_ADDRESS
);

  u_ALU u_alu_1 ();  // open: ALU_X, ALU_Y, ALU_RESULT, ALU_CONTROL
  u_MEM u_mem_1 ();  // open: ADDRESS, WORD_MODE, MEM_WRITE, DATA_IN, CLOCK, DATA_OUT

  // Notes on the sheet:
  //   Feel free to use these ALU/MEM components, or delete them!
endmodule

module u_ALU (
  input  [31:0] ALU_X,
  input  [31:0] ALU_Y,
  output [31:0] ALU_RESULT,
  output [3:0] ALU_CONTROL
);

  u_REV u_rev_1 ();  // open: INPUT, REVERSE_AMOUNT, OUTPUT

  // Notes on the sheet:
  //   Feel free to use this component, or not, however you want!
endmodule

// Data Memory
module u_MEM (
  input  [24:0] ADDRESS,
  input  WORD_MODE,
  input  MEM_WRITE,
  input  [31:0] DATA_IN,
  input  CLOCK,
  output [31:0] DATA_OUT
);


  // Notes on the sheet:
  //   Feel free to use this component, or not, however you want!
  //   You might use the word mode input to differentiate LW/SW from LH/SH.
  //   However, you *SHOULD* use 2 RAM modules, one for even addresses and one for odd addresses.
endmodule

module u_REV (
  input  [31:0] INPUT,
  input  [4:0] REVERSE_AMOUNT,
  output [31:0] OUTPUT
);


  // Notes on the sheet:
  //   Feel free to use this component, or not, however you want!
endmodule

module u_DECODE (
  input  [31:0] INSTRUCTION,
  output [3:0] OPCODE,
  output IMMEDIATEFLAG,
  output [4:0] RD,
  output [4:0] RS,
  output [4:0] RI,
  output [16:0] IMM,
  output [2:0] JC,
  output [23:0] ADDR
);


  assign ADDR = INSTRUCTION[23:0];
  assign IMM = INSTRUCTION[16:0];
  assign IMMEDIATEFLAG = INSTRUCTION[27];
  assign OPCODE = INSTRUCTION[31:28];
  assign RD = INSTRUCTION[26:22];
  assign RI = INSTRUCTION[4:0];
  assign RS = INSTRUCTION[21:17];

  // Other names for the same wires on the sheet: ADDRT[23:0] = INSTRUCTION[23:0];
  //   IMMEDIATET[16:0] = INSTRUCTION[16:0]; INSTRUCT[31:0] = INSTRUCTION; RIT[4:0] = INSTRUCTION[4:0];
  //   RST[4:0] = INSTRUCTION[21:17]; RDT[4:0] = INSTRUCTION[26:22]; JCT[2:0] = INSTRUCTION[26:24];
  //   IMMEDIATEFLAGT = INSTRUCTION[27]; OPCODET[3:0] = INSTRUCTION[31:28]
endmodule
